# Fritzing sketch BlinkNRF24L01 (saved by Fritzing 1.0.1rc)

parts:
  Componente1 = Arduino Uno (Rev3)
  Componente2 = Arduino Mega ADK (Rev3)
  Componente3 = NRF24L01+ Breakout Board
  Componente4 = NRF24L01+ Breakout Board

nets:
  N1: Componente1.D9_PWM, Componente4.CE
  N2: Componente1.D10_PWM/SS, Componente4.CS
  N3: Componente1.D11_PWM/MOSI, Componente4.MOSI
  N4: Componente1.D12/MISO, Componente4.MISO
  N5: Componente1.D13/SCK, Componente4.SCK
  3V3: Componente1.3V3, Componente4.VCC
  GND: Componente1.GND, Componente4.GND
  33V: Componente2.3V3, Componente3.VCC
  GND_2: Componente2.GND, Componente3.GND
  Chip Select: Componente2.D40, Componente3.CS
  Chip Enable: Componente2.D46, Componente3.CE
  MISO: Componente2.D50/MISO, Componente3.MISO
  MOSI: Componente2.D51/MOSI, Componente3.MOSI
  SCK: Componente2.D52/SCK, Componente3.SCK

// code stored in the sketch: BlinkNRF24L01.ino
/* ******************************************************************************************
Este é um projeto de "Hello World!" para testar os módulos de radiofrequencia NRF24L01
 Prof. Cleber Borges do canal FunBots: https://www.youtube.com/@FunBots
 ******************************************************************************************


/* ******************************************************************************************
 Aqui começa o código para o Receptor que deve ser carregado apenas no Arduino receptor
 ******************************************************************************************/

#include <RF24.h>

RF24 radio(9,10); // CE e CSN no arduino UNO - Arduio 
const byte address[6] ="00001"; // ambos devem ter configurado o mesmo endereço para estabelecerem a comunicação


void setup() {
  radio.begin(); //Iniciamos comunicação via Radio
  radio.openWritingPipe(address); //Abrimos o Pipe de comunicação para escrita
  radio.setPALevel(RF24_PA_MIN); 
	/*Definimos o PA Level low para prevenir possíveis problmas de corrente
  dado que estes testes são realizados geralmente numa bancada com os rádios bem próximos.*/
  radio.stopListening(); // Este módulo apenas realizará o envio do Hello World, por tanto não precisa "escutar"
}
  

void loop() {
  const char text[] = "Hello World!"; // Criamos uma constante tipo texto para armazenar a mensagem que será enviada
  radio.write(&text, sizeof(text)); 
	// Envia a mensagem de 
  delay(1000); // é um simples teste, então sim. Delay mesmo para simplificar.
}


/******************************************************************************************
// Aqui começa o código para o Receptor que deve ser carregado apenas no Arduino receptor
// ******************************************************************************************/

#include <RF24.h>


RF24 radio(46,40); // CE e CSN no arduno MEGA - Aduino Mega atua como receptor

const byte address[6] ="00001"; // ambos devem ter configurado o mesmo endereço para estabelecerem a comunicação

void setup() {
  Serial.begin(9600); // Iniciamos o Serial para podermos visualizar a mensagem
  Serial.print("Iniciando..."); 


  radio.begin(); //Iniciamos comunicação via Radio
  radio.openReadingPipe(0, address); //Abrimos o Pipe de comunicação para leitura
  radio.setPALevel(RF24_PA_MIN);
	/*Definimos o PA Level low para prevenir possíveis problmas de corrente
  dado que estes testes são realizados geralmente numa bancada com os rádios bem próximos.*/
  radio.startListening(); // Este módulo apenas realizará o recebimento da mensagem, por tanto não precisa "escutar"
}


void loop() {
  if(radio.available()){ //Verificamos que quando a mensagem tenha sido recebida, ele da True e executa o código a seguir
    char text[32] = ""; // instancia uma variável em branco
    radio.read(&text, sizeof(text)); //recebe a mensagem via radio e armazena na variável text
    Serial.println(text);// imprime a variável no terminal para podermos visualizar e validar que a comunicação está funcionando.
  }
}
